# Fritzing sketch Microphones (saved by Fritzing 0.9.4)
breadboards: 1

parts:
  Argon1 = Particle Argon
  Part1 = Adafruit MAX4466 Electret Microphone Amplifier [part_number="Adafruit #1063"]
  Part2 = Adafruit MAX4466 Electret Microphone Amplifier [part_number="Adafruit #1063"]
  Part3 = Adafruit MAX4466 Electret Microphone Amplifier [part_number="Adafruit #1063"]
  Part4 = Adafruit MicroSD card breakout board [part_number="Adafruit #254"]
  WS2812B1 = WS2812B NP [package="DIP (Dual Inline) [THT]"]
  WS2812B2 = WS2812B NP [package="DIP (Dual Inline) [THT]"]

nets:
  VCC: Argon1.3.3V, Part1.VCC, Part2.VCC, Part3.VCC, Part4.VCC, WS2812B1.5V, WS2812B2.5V
  GND: Argon1.GND, Part1.GND, Part2.GND, Part3.GND, Part4.GND, WS2812B1.GND, WS2812B2.GND
  N1: Argon1.A0, Part1.OUT
  N2: Argon1.A1, Part2.OUT
  N3: Argon1.A2, Part3.OUT
  N4: Argon1.A3, WS2812B2.DI
  N5: Argon1.A4, WS2812B1.DI
  N6: Argon1.A5, Part4.CS
  N7: Argon1.SCK, Part4.CLK
  N8: Argon1.MO, Part4.DI
  N9: Argon1.MI, Part4.DO

custom parts:
  Particle Argon: The Argon is a powerful Wi-Fi enabled development board that can act as either a standalone Wi-Fi endpoint or Wi-Fi enabled gateway for Particle Mesh networks. It is based on the Nordic nRF52840 and has built-in battery charging circuitry so it’s easy to connect a Li-Po and deploy your local network in minutes. The Argon is great for connecting existing projects to the Particle Device Cloud or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
  Adafruit MAX4466 Electret Microphone Amplifier: Add an ear to your project with this well-designed electret microphone amplifier. This fully assembled and tested board comes with a 20-20KHz electret microphone soldered on. For the amplification, we use the Maxim MAX4466, an op-amp specifically designed for this delicate task! The amplifier has excellent power supply noise rejection, so this amplifier sounds really good and isn't nearly as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
  Adafruit MicroSD card breakout board: Not just a simple breakout board, this microSD adapter goes the extra mile - designed for ease of use. Onboard 5v->3v regulator provides 150mA for power-hungry cards 3v level shifting means you can use this with ease on either 3v or 5v systems Uses a proper level shifting chip, not resistors: less problems, and faster read/write access Use 3 or 4 digital pins to read and write 2Gb+ of storage!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
  WS2812B NP: WS2812B Adafruit Breakout Neopixel
